// Logisim project CPLD.circ as structural Verilog: 8 circuits, main circuit main
module main (
  input  CLK,
  input  MSG
);

  wire and_1_out, and_2_out, and_3_out, bcd_to_7segment_1_a, bcd_to_7segment_1_b, bcd_to_7segment_1_c,
       bcd_to_7segment_1_d, bcd_to_7segment_1_e, bcd_to_7segment_1_f, bcd_to_7segment_1_g,
       bcd_to_7segment_2_a, bcd_to_7segment_2_b, bcd_to_7segment_2_c, bcd_to_7segment_2_d,
       bcd_to_7segment_2_e, bcd_to_7segment_2_f, bcd_to_7segment_2_g, bit_counter_1_d0, bit_counter_1_d1,
       bit_counter_1_d2, bit_counter_1_d3, clock_divider_1_clk1, clock_divider_1_clk2, D0_1, D0_2, D1_1,
       D1_2, D2_1, D2_2, D3_1, D3_2, not_1_out, not_2_out, not_3_out, or_1_out, shift_register_1_d0,
       shift_register_1_d1, shift_register_1_d2, shift_register_1_d3, shift_register_1_d4,
       shift_register_1_d5, shift_register_1_d6, shift_register_1_d7, state_machine_1_q_startbit;

  and and_1 (and_1_out, or_1_out, clock_divider_1_clk1);
  or or_1 (or_1_out, and_3_out, ~state_machine_1_q_startbit);  // OR_Gate
  state_machine state_machine_1 (.Message(MSG), .CLK(and_1_out), .q_startbit(state_machine_1_q_startbit));
  clock_divider clock_divider_1 (.CLK(CLK), .CLK1(clock_divider_1_clk1), .CLK2(clock_divider_1_clk2));
  and and_2 (and_2_out, state_machine_1_q_startbit, clock_divider_1_clk2);
  bcd_to_7segment bcd_to_7segment_1 (
    .D3(D3_2), .D2(D2_2), .D1(D1_2), .D0(D0_2), .a(bcd_to_7segment_1_a), .d(bcd_to_7segment_1_d),
    .b(bcd_to_7segment_1_b), .e(bcd_to_7segment_1_e), .c(bcd_to_7segment_1_c), .f(bcd_to_7segment_1_f),
    .g(bcd_to_7segment_1_g));
  not not_1 (not_1_out, state_machine_1_q_startbit);
  _7_Segment_Display L_7_Segment_Display_1 (
    .g(bcd_to_7segment_1_g), .f(bcd_to_7segment_1_f), .a(bcd_to_7segment_1_a), .b(bcd_to_7segment_1_b),
    .e(bcd_to_7segment_1_e), .d(bcd_to_7segment_1_d), .c(bcd_to_7segment_1_c));  // open: dp
  and and_3 (and_3_out, bit_counter_1_d0, not_2_out, not_3_out, bit_counter_1_d3);
  not not_2 (not_2_out, bit_counter_1_d1);
  not not_3 (not_3_out, bit_counter_1_d2);
  bit_counter bit_counter_1 (
    .CLK(and_2_out), .CLR(not_1_out), .D0(bit_counter_1_d0), .D1(bit_counter_1_d1), .D2(bit_counter_1_d2),
    .D3(bit_counter_1_d3));
  shift_register shift_register_1 (
    .Message(MSG), .CLK(clock_divider_1_clk2), .D7(shift_register_1_d7), .D6(shift_register_1_d6),
    .D5(shift_register_1_d5), .D4(shift_register_1_d4), .D3(shift_register_1_d3), .D2(shift_register_1_d2),
    .D1(shift_register_1_d1), .D0(shift_register_1_d0));
  D_Flip_Flop d_ff_1 (.D(shift_register_1_d3), .clk(and_3_out), .Q(D3_1));  // open: Qn, preset, reset
  D_Flip_Flop d_ff_2 (.D(shift_register_1_d2), .clk(and_3_out), .Q(D2_1));  // open: Qn, preset, reset
  D_Flip_Flop d_ff_3 (.D(shift_register_1_d1), .clk(and_3_out), .Q(D1_1));  // open: Qn, preset, reset
  D_Flip_Flop d_ff_4 (.D(shift_register_1_d0), .clk(and_3_out), .Q(D0_1));  // open: Qn, preset, reset
  D_Flip_Flop d_ff_5 (.D(shift_register_1_d7), .clk(and_3_out), .Q(D3_2));  // open: Qn, preset, reset
  D_Flip_Flop d_ff_6 (.D(shift_register_1_d6), .clk(and_3_out), .Q(D2_2));  // open: Qn, preset, reset
  D_Flip_Flop d_ff_7 (.D(shift_register_1_d5), .clk(and_3_out), .Q(D1_2));  // open: Qn, preset, reset
  D_Flip_Flop d_ff_8 (.D(shift_register_1_d4), .clk(and_3_out), .Q(D0_2));  // open: Qn, preset, reset
  bcd_to_7segment bcd_to_7segment_2 (
    .D3(D3_1), .D2(D2_1), .D1(D1_1), .D0(D0_1), .a(bcd_to_7segment_2_a), .d(bcd_to_7segment_2_d),
    .b(bcd_to_7segment_2_b), .e(bcd_to_7segment_2_e), .c(bcd_to_7segment_2_c), .f(bcd_to_7segment_2_f),
    .g(bcd_to_7segment_2_g));
  _7_Segment_Display L_7_Segment_Display_2 (
    .g(bcd_to_7segment_2_g), .f(bcd_to_7segment_2_f), .a(bcd_to_7segment_2_a), .b(bcd_to_7segment_2_b),
    .e(bcd_to_7segment_2_e), .d(bcd_to_7segment_2_d), .c(bcd_to_7segment_2_c));  // open: dp

  // Notes on the sheet:
  //   Problem When There is no Stop Bit
endmodule

module state_machine (
  input  Message,
  input  CLK,
  output q_startbit
);

  wire and_1_out, and_2_out, and_3_out, and_4_out, d_ff_1_qn, d_ff_2_q, d_ff_3_q, d_ff_3_qn, not_1_out,
       or_1_out, xor_1_out;

  not not_1 (not_1_out, Message);
  and and_1 (and_1_out, or_1_out, not_1_out);
  or or_1 (or_1_out, and_2_out, q_startbit);
  D_Flip_Flop d_ff_1 (.D(and_1_out), .clk(CLK), .Q(q_startbit), .Qn(d_ff_1_qn));  // open: preset, reset
  xor xor_1 (xor_1_out, d_ff_3_q, d_ff_2_q);
  and and_2 (and_2_out, d_ff_3_q, d_ff_2_q);
  D_Flip_Flop d_ff_2 (.D(and_3_out), .clk(CLK), .Q(d_ff_2_q));  // open: Qn, preset, reset
  and and_3 (and_3_out, xor_1_out, not_1_out);
  D_Flip_Flop d_ff_3 (.D(and_4_out), .clk(CLK), .Q(d_ff_3_q), .Qn(d_ff_3_qn));  // open: preset, reset
  and and_4 (and_4_out, d_ff_3_qn, d_ff_1_qn, not_1_out);
endmodule

module bit_counter (
  input  CLK,
  input  CLR,
  output D0,
  output D1,
  output D2,
  output D3
);

  wire and_1_out, and_2_out, and_3_out, and_4_out, and_5_out, and_6_out, and_7_out, and_8_out, or_1_out,
       or_2_out, or_3_out, Q0n, Q1n, Q2n, Q3n, xor_1_out;

  D_Flip_Flop d_ff_1 (.D(Q0n), .clk(CLK), .Q(D0), .Qn(Q0n), .reset(or_1_out));  // open: preset
  or or_1 (or_1_out, and_1_out, CLR);
  and and_1 (and_1_out, Q0n, D1, Q2n, D3);
  xor xor_1 (xor_1_out, Q0n, Q1n);
  D_Flip_Flop d_ff_2 (.D(xor_1_out), .clk(CLK), .Q(D1), .Qn(Q1n), .reset(or_1_out));  // open: preset
  and and_2 (and_2_out, D0, D1, Q2n);
  and and_3 (and_3_out, Q1n, D2);
  and and_4 (and_4_out, Q0n, D2);
  or or_2 (or_2_out, and_2_out, and_3_out, and_4_out);
  D_Flip_Flop d_ff_3 (.D(or_2_out), .clk(CLK), .Q(D2), .Qn(Q2n));  // open: preset, reset
  and and_5 (and_5_out, D3, Q0n);
  D_Flip_Flop d_ff_4 (.D(or_3_out), .clk(CLK), .Q(D3), .Qn(Q3n), .reset(or_1_out));  // open: preset
  and and_6 (and_6_out, D3, Q1n);
  and and_7 (and_7_out, D3, Q2n);
  or or_3 (or_3_out, and_5_out, and_6_out, and_7_out, and_8_out);
  and and_8 (and_8_out, D0, D1, D2, Q3n);

  // Other names for the same wires on the sheet: Q0 = D0; Q1 = D1; Q2 = D2; Q3 = D3
endmodule

module shift_register (
  input  Message,
  input  CLK,
  output D7,
  output D6,
  output D5,
  output D4,
  output D3,
  output D2,
  output D1,
  output D0
);

  D_Flip_Flop d_ff_1 (.D(Message), .clk(CLK), .Q(D7));  // open: Qn, preset, reset
  D_Flip_Flop d_ff_2 (.D(D7), .clk(CLK), .Q(D6));  // open: Qn, preset, reset
  D_Flip_Flop d_ff_3 (.D(D6), .clk(CLK), .Q(D5));  // open: Qn, preset, reset
  D_Flip_Flop d_ff_4 (.D(D5), .clk(CLK), .Q(D4));  // open: Qn, preset, reset
  D_Flip_Flop d_ff_5 (.D(D4), .clk(CLK), .Q(D3));  // open: Qn, preset, reset
  D_Flip_Flop d_ff_6 (.D(D3), .clk(CLK), .Q(D2));  // open: Qn, preset, reset
  D_Flip_Flop d_ff_7 (.D(D2), .clk(CLK), .Q(D1));  // open: Qn, preset, reset
  D_Flip_Flop d_ff_8 (.D(D1), .clk(CLK), .Q(D0));  // open: Qn, preset, reset
endmodule

module clock_divider (
  input  CLK,
  output CLK1,
  output CLK2
);

  wire d_ff_1_q, d_ff_1_qn, d_ff_2_qn, d_ff_3_q, d_ff_3_qn, d_ff_4_q, d_ff_4_qn, d_ff_5_qn;

  D_Flip_Flop d_ff_1 (.D(d_ff_1_qn), .clk(CLK), .Q(d_ff_1_q), .Qn(d_ff_1_qn));  // open: preset, reset
  D_Flip_Flop d_ff_2 (.D(d_ff_2_qn), .clk(d_ff_1_qn), .Q(CLK1), .Qn(d_ff_2_qn));  // open: preset, reset
  D_Flip_Flop d_ff_3 (.D(d_ff_3_qn), .clk(d_ff_2_qn), .Q(d_ff_3_q), .Qn(d_ff_3_qn));  // open: preset, reset
  D_Flip_Flop d_ff_4 (.D(d_ff_4_qn), .clk(d_ff_3_qn), .Q(d_ff_4_q), .Qn(d_ff_4_qn));  // open: preset, reset
  D_Flip_Flop d_ff_5 (.D(d_ff_5_qn), .clk(d_ff_4_qn), .Q(CLK2), .Qn(d_ff_5_qn));  // open: preset, reset
endmodule

module bcd_to_7segment (
  input  D3,
  input  D2,
  input  D1,
  input  D0,
  output a,
  output d,
  output b,
  output e,
  output c,
  output f,
  output g
);

  wire An, and_1_out, and_2_out, and_3_out, and_4_out, and_5_out, and_6_out, and_7_out, and_8_out, and_9_out,
       and_10_out, and_11_out, and_12_out, and_13_out, and_14_out, and_15_out, and_16_out, Bn, Cn, Dn;

  not not_1 (An, D3);
  not not_2 (Bn, D2);
  not not_3 (Cn, D1);
  not not_4 (Dn, D0);
  and and_1 (and_1_out, D2, D0);
  and and_2 (and_2_out, Bn, Dn);
  and and_3 (and_3_out, Cn, Dn);
  and and_4 (and_4_out, D1, D0);
  or or_1 (a, and_2_out, D1, D3, and_1_out);
  or or_2 (b, and_3_out, Bn, and_4_out);
  or or_3 (c, Cn, D0, D2);
  and and_5 (and_5_out, Bn, D1);
  and and_6 (and_6_out, D2, Cn);
  and and_7 (and_7_out, D2, Dn);
  and and_8 (and_8_out, Bn, D1);
  or or_4 (g, and_5_out, and_6_out, and_7_out, D3);
  and and_9 (and_9_out, Bn, Dn);
  and and_10 (and_10_out, D2, Cn, D0);
  and and_11 (and_11_out, D1, Dn);
  and and_12 (and_12_out, Bn, Dn);
  and and_13 (and_13_out, D1, Dn);
  and and_14 (and_14_out, Cn, Dn);
  and and_15 (and_15_out, Cn, D2);
  and and_16 (and_16_out, Dn, D2);
  or or_5 (d, and_9_out, and_8_out, and_10_out, and_11_out, D3);
  or or_6 (e, and_12_out, and_13_out);
  or or_7 (f, and_14_out, and_15_out, and_16_out, D3);

  // Other names for the same wires on the sheet: A_t = D3; B_t = D2; C_t = D1; D_t = D0
endmodule

module memory_read_write (
  input  in_1
);
endmodule

module coc_divider (
  input  CLK,
  output CLK2
);

  wire d_ff_1_q, d_ff_1_qn, d_ff_2_q, d_ff_2_qn, d_ff_3_qn;

  D_Flip_Flop d_ff_1 (.D(d_ff_1_qn), .clk(CLK), .Q(d_ff_1_q), .Qn(d_ff_1_qn));  // open: preset, reset
  D_Flip_Flop d_ff_2 (.D(d_ff_2_qn), .clk(d_ff_1_qn), .Q(d_ff_2_q), .Qn(d_ff_2_qn));  // open: preset, reset
  D_Flip_Flop d_ff_3 (.D(d_ff_3_qn), .clk(d_ff_2_qn), .Q(CLK2), .Qn(d_ff_3_qn));  // open: preset, reset
endmodule
